# Fritzing sketch sketch (saved by Fritzing 0.9.3b)
stripboards: 1

parts:
  IC1 = ULN2803A [package=THT]
  U4 = Voltage Regulator [package=to220-igo]
  C2 = Ceramic Capacitor [capacitance=100nF voltage=20V package="100 mil [THT, multilayer]"]
  C3 = Ceramic Capacitor [capacitance=100nF voltage=20V package="100 mil [THT, multilayer]"]
  C4 = Electrolytic Capacitor [capacitance=10µF package="100 mil [THT, electrolytic]"]
  D1 = Rectifier Diode [part_number=1N4001 package="300 mil [THT]"]
  J2 = double row male pin header, 8 pins [form="♂ (male)"]
  IC2 = ULN2803A [package=THT]
  J3 = double row male pin header, 8 pins [form="♂ (male)"]
  J1 = double row male pin header, 2 pins [form="♂ (male)"]
  J9 = female pin header, 4 pins [form="♀ (female)"]
  J10 = female pin header, 4 pins [form="♀ (female)"]
  J11 = female pin header, 1 pin [form="♀ (female)"]
  J12 = female pin header, 4 pins [form="♀ (female)"]
  J13 = female pin header, 4 pins [form="♀ (female)"]
  J14 = female pin header, 1 pin [form="♀ (female)"]
  J15 = double row male pin header, 2 pins [form="♂ (male)"]

nets:
  N1: IC1.In_1, J10.pin1
  N2: IC1.In_2, J10.pin2
  N3: IC1.In_3, J10.pin3
  N4: IC1.In_4, J10.pin4
  N5: IC1.In_5, J9.pin4
  N6: IC1.In_6, J9.pin1
  N7: IC1.In_7, J9.pin2
  N8: IC1.In_8, J9.pin3
  N9: IC1.0V, IC1.COM_-_Common, U4.IN, C2.0, C3.1, C4.-, IC2.0V, J1.pin1, J11.pin1, J15.pin2
  N10: IC1.Out_8, J2.pin8
  N11: IC1.Out_7, J2.pin7
  N12: IC1.Out_6, J2.pin6
  N13: IC1.Out_5, J2.pin5
  N14: IC1.Out_4, J2.pin4
  N15: IC1.Out_3, J2.pin3
  N16: IC1.Out_2, J2.pin2
  N17: IC1.Out_1, J2.pin1
  N18: U4.GND, C3.0, C4.+, D1.cathode
  N19: U4.OUT, C2.1, J1.pin2
  N20: D1.anode, J15.pin1
  N21: IC2.In_1, J12.pin1
  N22: IC2.In_2, J12.pin2
  N23: IC2.In_3, J12.pin3
  N24: IC2.In_4, J12.pin4
  N25: IC2.In_5, J13.pin4, J14.pin1
  N26: IC2.In_6, J13.pin1
  N27: IC2.In_7, J13.pin2
  N28: IC2.In_8, J13.pin3
  N29: IC2.Out_8, J3.pin8
  N30: IC2.Out_7, J3.pin7
  N31: IC2.Out_6, J3.pin6
  N32: IC2.Out_5, J3.pin5
  N33: IC2.Out_4, J3.pin4
  N34: IC2.Out_3, J3.pin3
  N35: IC2.Out_2, J3.pin2
  N36: IC2.Out_1, J3.pin1

notes:
  12V
  in
  LED-
  0-7
  LED-
  9-15
  5V
  out
